# Fritzing sketch RP2040-Thermohygrometer-Deluxe (saved by Fritzing 1.0.5)
breadboards: 1

parts:
  AHT1 = AHT20 BMP280 pressure and humidity breakout
  A1 = Waveshare rp2040-zero smd [package=SMD]
  S1 = 0.91 inch OLED I2C Display 128 x 32 Pixels
  S2 = 0.91 inch OLED I2C Display 128 x 32 Pixels
  S3 = 0.91 inch OLED I2C Display 128 x 32 Pixels
  S5 = Momentary Switch 6mm 2pin

nets:
  VCC: AHT1.VDD, A1.Pin_3, S1.VCC, S2.VCC, S3.VCC
  N1: AHT1.SDA, A1.Pin_5, S2.SDA
  GND: AHT1.GND, A1.Pin_2, A1.Pin_33, S1.GND, S2.GND, S3.GND, S5.2
  N2: AHT1.SCL, A1.Pin_9, S2.SCL
  N3: A1.Pin_4, S5.1
  N4: A1.Pin_15, S1.SCL
  N5: A1.Pin_16, S1.SDA
  N6: A1.Pin_17, S3.SCL
  N7: A1.Pin_18, S3.SDA

notes:
  温湿度・気圧センサーモジュール
  OLED モジュール x3
  RP2040-Zero
  ブレッドボード 400H
  タクトスイッチ

custom parts:
  AHT20 BMP280 pressure and humidity breakout: Cheap breakout board for the BMP280, barometric pressure sensor, and AHT20, humidity sensor
  Waveshare rp2040-zero smd: .RP2040-Zero, A Low-Cost, High-Performance Pico-Like MCU Board Based On Raspberry Pi Microcontroller RP2040. This varant is SMD with all the connections.
  Momentary Switch 6mm 2pin: Momentary Switch 6mm 2 pin Button commonly used for reset or general input.
